// Logisim project Somatorio.circ as structural Verilog: 1 circuit, main circuit main
module main (
  input  [3:0] A,
  input  [3:0] B,
  output [3:0] S,
  output Cout
);

  wire main_1_cout, main_2_cout, main_3_cout, xor_1_out, xor_2_out, xor_3_out, xor_4_out;

  xor xor_1 (xor_1_out, 1'b0, B[0]);
  xor xor_2 (xor_2_out, 1'b0, B[1]);
  xor xor_3 (xor_3_out, 1'b0, B[2]);
  xor xor_4 (xor_4_out, 1'b0, B[3]);
  Full_adder_main main_1 (.Cin(1'b0), .A(A[0]), .B(xor_1_out), .S(S[0]), .Cout(main_1_cout));
  Full_adder_main main_2 (.Cin(main_1_cout), .A(A[1]), .B(xor_2_out), .S(S[1]), .Cout(main_2_cout));
  Full_adder_main main_3 (.Cin(main_2_cout), .A(A[2]), .B(xor_3_out), .S(S[2]), .Cout(main_3_cout));
  Full_adder_main main_4 (.Cin(main_3_cout), .A(A[3]), .B(xor_4_out), .S(S[3]), .Cout(Cout));
endmodule
