// Logisim project Full adder.circ as structural Verilog: 1 circuit, main circuit main
module main (
  input  Cin,
  input  A,
  input  B,
  output S,
  output Cout
);

  wire main_1_c, main_1_s, main_2_c;

  Half_adder_main main_1 (.A(A), .B(B), .S(main_1_s), .C(main_1_c));
  Half_adder_main main_2 (.A(Cin), .B(main_1_s), .S(S), .C(main_2_c));
  or or_1 (Cout, main_2_c, main_1_c);
endmodule
