// Logisim project circuito_mem_d.circ as structural Verilog: 1 circuit, main circuit main
module main (
  input  reset,
  output EN_PC,
  output [1:0] Sel_0,
  output [3:0] Output,
  output Op_FSM,
  output [1:0] Sel_1,
  output Sel_2
);

  wire and_1_out, and_2_out, and_3_out, and_4_out, and_5_out, and_6_out, and_7_out, and_8_out, clock_1_out,
       not_1_out, or_1_out, or_5_out, St0_q, St0_qn, St1_q, St1_qn, St2_qn;
  wire [3:0] adder_1_out, counter_1_q, multiplexer_1_out, multiplexer_2_out, Reg_SOMA_q, Reg_SUB_q,
       subtractor_1_out;
  wire [7:0] ram_1_data;

  and and_1 (and_1_out, and_3_out, not_1_out);
  or or_1 (or_1_out, and_1_out, and_4_out);
  and and_2 (and_2_out, St0_q, St1_q);
  Clock clock_1 (.out(clock_1_out));
  and and_3 (and_3_out, St0_qn, St2_qn);
  not not_1 (not_1_out, Op_FSM);
  and and_4 (and_4_out, St1_q, St0_qn);
  D_Flip_Flop St2 (.clk(clock_1_out), .D(and_2_out), .Q(Sel_0[0]), .Qn(St2_qn));  // open: preset, en, reset
  and and_5 (and_5_out, St1_qn, St0_q);
  or or_2 (Sel_0[1], Sel_0[0], St0_q);
  or or_3 (Sel_1[0], St0_q, St1_qn);
  and and_6 (and_6_out, St0_qn, St2_qn);
  or or_4 (EN_PC, and_5_out, Sel_0[0]);
  and and_7 (and_7_out, and_6_out, Op_FSM);
  or or_5 (or_5_out, and_7_out, and_8_out);
  and and_8 (and_8_out, St1_q, St0_qn);
  D_Flip_Flop St1 (.clk(clock_1_out), .D(or_5_out), .Q(St1_q), .Qn(St1_qn));  // open: preset, en, reset
  Counter #(.width(4), .max('hf)) counter_1 (
    .count(EN_PC), .Q(counter_1_q), .clk(clock_1_out), .clr(reset));  // open: load, D, carry
  D_Flip_Flop St0 (.clk(clock_1_out), .D(or_1_out), .Q(St0_q), .Qn(St0_qn));  // open: preset, en, reset
  RAM #(.addrWidth(4), .dataWidth(9)) ram_1 (
    .addr(counter_1_q), .data({Op_FSM, ram_1_data}), .clr(reset));  // open: sel, clk, ld
  Multiplexer #(.select(2), .width(4), .enable("false")) multiplexer_1 (
    .in0(ram_1_data[3:0]), .in1(ram_1_data[7:4]), .in2(Reg_SOMA_q), .in3(Reg_SUB_q), .out(multiplexer_1_out),
    .sel(Sel_0));
  Multiplexer #(.select(2), .width(4), .enable("false")) multiplexer_2 (
    .in0(ram_1_data[3:0]), .in1(ram_1_data[7:4]), .in2(Reg_SOMA_q), .in3(Reg_SUB_q), .out(multiplexer_2_out),
    .sel({1'b0, Sel_1[0]}));
  Adder #(.width(4)) adder_1 (.a(multiplexer_1_out), .b(multiplexer_2_out), .out(adder_1_out));  // open: cin, cout
  Subtractor #(.width(4)) subtractor_1 (
    .a(multiplexer_1_out), .b(multiplexer_2_out), .out(subtractor_1_out));  // open: bin, bout
  Register #(.width(4)) Reg_SOMA (.D(adder_1_out), .Q(Reg_SOMA_q), .clk(clock_1_out), .clr(reset));  // open: en
  Register #(.width(4)) Reg_SUB (.D(subtractor_1_out), .Q(Reg_SUB_q), .clk(clock_1_out), .clr(reset));  // open: en
  Multiplexer #(.width(4), .enable("false")) multiplexer_3 (
    .in0(Reg_SOMA_q), .in1(Reg_SUB_q), .out(Output), .sel(1'b1));

  assign Sel_1[1] = 1'b0;
  assign Sel_2 = 1'b1;

  // Notes on the sheet:
  //   0 = (a+b) - b
  //   1 = a + a - b - b
endmodule
